// Logisim project assignment_2_Logisim project.circ as structural Verilog
module P1_and_or (
  input  a,
  input  b,
  input  c,
  input  d,
  output out1,
  output out2
);

  logic4 logic4_1 (.a(a), .b(b), .c(c), .d(d), .out1(out1), .out2(out2));
endmodule

module P2_mux8_1 (
  input  d0,
  input  d1,
  input  d2,
  input  d3,
  input  d4,
  input  d5,
  input  d6,
  input  d7,
  input  [2:0] ch,
  output data
);

  mux8_1 mux8_1_1 (.d0(d0), .d1(d1), .d2(d2), .d3(d3), .d4(d4), .d5(d5), .d6(d6), .d7(d7), .ch(ch), .data(data));
endmodule

module P3_letter (
  input  en,
  input  [2:0] sel,
  output [7:0] display
);

  letter_led letter_led_1 (.en(en), .sel(sel), .display(display));
  _7_Segment_Display u_7_segment_display_1 (
    .g(display[1]), .f(display[2]), .a(display[7]), .b(display[6]), .e(display[3]), .d(display[4]),
    .c(display[5]), .dp(display[0]));
endmodule

module P4_vote25 (
  input  [24:0] vt,
  output result
);

  vote25 vote25_1 (.vt(vt), .result(result));
endmodule

module P5_count13 (
  input  en,
  input  [12:0] vt,
  output [7:0] display
);

  count13_led count13_led_1 (.en(en), .vt(vt), .display(display));
  _7_Segment_Display u_7_segment_display_1 (
    .g(display[1]), .f(display[2]), .a(display[7]), .b(display[6]), .e(display[3]), .d(display[4]),
    .c(display[5]), .dp(display[0]));
endmodule

// VHDL entity logic4, as the project stores it:
--library and package
library ieee;
use ieee.std_logic_1164.all;
use ieee.std_logic_arith.all;
use ieee.std_logic_unsigned.all;

--entity
entity logic4 is
     port(
          a,b,c,d    :in  std_logic;
          out1,out2  :out std_logic
     );
end entity logic4;

--architecture
architecture bhv of logic4 is
begin
     out1 <= a and b and c and d;   -- 4-input AND
     out2 <= a or b or c or d;      -- 4-input OR
end architecture bhv;

// VHDL entity mux8_1, as the project stores it:
--library and package
library ieee;
use ieee.std_logic_1164.all;
use ieee.std_logic_arith.all;
use ieee.std_logic_unsigned.all;

--entity
entity mux8_1 is
     port(
          d0,d1,d2,d3,d4,d5,d6,d7 :in  std_logic;
          ch                      :in  std_logic_vector(2 downto 0);
          data                    :out std_logic
     );
end entity mux8_1;

--architecture
architecture bhv of mux8_1 is
begin
     process(d0,d1,d2,d3,d4,d5,d6,d7,ch)
     begin
          case ch is
               when "000"  => data <= d0;
               when "001"  => data <= d1;
               when "010"  => data <= d2;
               when "011"  => data <= d3;
               when "100"  => data <= d4;
               when "101"  => data <= d5;
               when "110"  => data <= d6;
               when "111"  => data <= d7;
               when others => data <= '0';
          end case;
     end process;
end architecture bhv;

// VHDL entity letter_led, as the project stores it:
--library and package
library ieee;
use ieee.std_logic_1164.all;
use ieee.std_logic_arith.all;
use ieee.std_logic_unsigned.all;

--entity
-- display(7 downto 0) = a b c d e f g dp
entity letter_led is
     port(
          en      :in  std_logic;
          sel     :in  std_logic_vector(2 downto 0);
          display :out std_logic_vector(7 downto 0)
     );
end entity letter_led;

--architecture
architecture bhv of letter_led is
begin
     process(en,sel)
     begin
          if en='0' then
               display <= "ZZZZZZZZ";
          else
               case sel is
                    when "000"  => display <= "11101110";  -- A
                    when "001"  => display <= "00111110";  -- b
                    when "010"  => display <= "10011100";  -- C
                    when "011"  => display <= "01111010";  -- d
                    when "100"  => display <= "10001110";  -- F
                    when "101"  => display <= "11110110";  -- g
                    when others => display <= "00000000";  -- off
               end case;
          end if;
     end process;
end architecture bhv;

// VHDL entity vote25, as the project stores it:
--library and package
library ieee;
use ieee.std_logic_1164.all;
use ieee.std_logic_arith.all;
use ieee.std_logic_unsigned.all;

--entity
entity vote25 is
     port(
          vt     :in  std_logic_vector(25 downto 1);
          result :out std_logic
     );
end entity vote25;

--architecture
architecture bhv of vote25 is
begin
     process(vt)
     variable sum:integer range 0 to 25;
     begin
          sum := 0;
          for i in 1 to 25 loop
               if (vt(i)='1') then
                    sum := sum+1;
               end if;
          end loop;
          if sum >= 13 then      -- more than half of 25
               result <= '1';
          else
               result <= '0';
          end if;
     end process;
end architecture bhv;

// VHDL entity count13_led, as the project stores it:
--library and package
library ieee;
use ieee.std_logic_1164.all;
use ieee.std_logic_arith.all;
use ieee.std_logic_unsigned.all;

--entity
-- display(7 downto 0) = a b c d e f g dp
entity count13_led is
     port(
          en      :in  std_logic;
          vt      :in  std_logic_vector(13 downto 1);
          display :out std_logic_vector(7 downto 0)
     );
end entity count13_led;

--architecture
architecture bhv of count13_led is
begin
     process(en,vt)
     variable sum:integer range 0 to 15;
     begin
          sum := 0;
          for i in 1 to 13 loop
               if (vt(i)='1') then
                    sum := sum+1;
               end if;
          end loop;
          if en='0' then
               display <= "00000000";               -- display off
          else
               case sum is
                    when 0      => display <= "11111100";  -- 0
                    when 1      => display <= "01100000";  -- 1
                    when 2      => display <= "11011010";  -- 2
                    when 3      => display <= "11110010";  -- 3
                    when 4      => display <= "01100110";  -- 4
                    when 5      => display <= "10110110";  -- 5
                    when 6      => display <= "10111110";  -- 6
                    when 7      => display <= "11100000";  -- 7
                    when 8      => display <= "11111110";  -- 8
                    when 9      => display <= "11110110";  -- 9
                    when 10     => display <= "11101110";  -- A
                    when 11     => display <= "00111110";  -- b
                    when 12     => display <= "10011100";  -- C
                    when 13     => display <= "01111010";  -- d
                    when 14     => display <= "10011110";  -- E
                    when 15     => display <= "10001110";  -- F
                    when others => display <= "00000000";
               end case;
          end if;
     end process;
end architecture bhv;
